# Fritzing sketch FinalBluetooth (saved by Fritzing 0.9.3b)
circuit board: 5.3874cm x 4.59284cm
breadboards: 1

parts:
  ArduinoNano = Arduino Nano (Rev3.0)
  HC-06 = Bluetooth HC-06u [package=THT]
  Q1 = PNP-Transistor [package="TO92 [THT]"]
  TRANSISTOR = NPN-Transistor [package="TO92 [THT]"]
  Q3 = NPN-Transistor [package="TO92 [THT]"]
  Q4 = NPN-Transistor [package="TO92 [THT]"]
  ElWire = female pin header, 2 pins [form="♀ (female)"]
  RGB = female pin header, 2 pins [form="♀ (female)"]
  rgb2 = female pin header, 2 pins [form="♀ (female)"]
  12V = female pin header, 2 pins [form="♀ (female)"]
  5V = female pin header, 2 pins [form="♀ (female)"]
  UV = female pin header, 2 pins [form="♀ (female)"]

nets:
  N1: ArduinoNano.D1/TX, HC-06.RXD
  N2: ArduinoNano.D0/RX, HC-06.TXD
  GND: ArduinoNano.GND, HC-06.GND, Q1.C, TRANSISTOR.C, Q3.C, Q4.C, 12V.pin1, 5V.pin2
  N3: ArduinoNano.D6, Q1.B
  N4: ArduinoNano.D9, TRANSISTOR.B
  N5: ArduinoNano.D10, Q3.B
  N6: ArduinoNano.D11/MOSI, Q4.B
  N7: ArduinoNano.VIN, 5V.pin1
  5V: ArduinoNano.5V, HC-06.VCC
  N8: Q1.E, ElWire.pin2, UV.pin2
  N9: TRANSISTOR.E, RGB.pin1
  N10: Q3.E, rgb2.pin2
  N11: Q4.E, rgb2.pin1
  N12: ElWire.pin1, RGB.pin2, 12V.pin2, UV.pin1

custom parts:
  Bluetooth HC-06u: Bluetooth HC-06 - face up, pins down 16.5mm x 37.5mm PCB
