# Fritzing sketch wemos_led (saved by Fritzing 0.9.3b)
perfboards: 1

parts:
  WeMos_D1_Mini2 = WeMos D1 Mini
  Q1 = npn-Powertransistor [package="TO220 [THT]"]
  Q2 = npn-Powertransistor [package="TO220 [THT]"]
  Q4 = npn-Powertransistor [package="TO220 [THT]"]
  J1 = female pin header, 2 pins [form="♀ (female)"]
  Q5 = npn-Powertransistor [package="TO220 [THT]"]

nets:
  N1: WeMos_D1_Mini2.5V, J1.pin1
  N2: WeMos_D1_Mini2.D1, Q4.base
  N3: WeMos_D1_Mini2.D2, Q2.base
  N4: WeMos_D1_Mini2.D7, Q5.base
  N5: WeMos_D1_Mini2.D8, Q1.base
  N6: WeMos_D1_Mini2.G, Q4.emitter, J1.pin2
